# Fritzing sketch Robgyak (saved by Fritzing 0.9.9b)
breadboards: 1

parts:
  Part1 = Arduino Micro (Rev3)
  Part2 = LCD1602-I2C
  S1 = Pushbutton [package="[THT]"]
  R1 = Resistor [tolerance=±5% power=0.25 resistance=10k package=THT]
  TTP223B1 = TTP223B Capacitive Touch Sensor Module
  LED1 = RGB LED (com. cathode, rgb) [package="5 mm [THT]"]
  R2 = Resistor [tolerance=±5% power=0.25 resistance=220 package=THT]
  R3 = Resistor [tolerance=±5% power=0.25 resistance=220 package=THT]
  R4 = Resistor [tolerance=±5% power=0.25 resistance=220 package=THT]
  e-radionica1 = TCS230 Color Sensor [part_number=101209]

nets:
  N1: Part1.D1/TX, e-radionica1.S2
  N2: Part1.D0/RX, e-radionica1.Out
  GND: Part1.GND, Part2.GND, R1.Pin_1, TTP223B1.GND, LED1.common_cathode, e-radionica1.Gnd
  VCC: Part1.5V, Part2.VCC, S1.Pin_3, S1.Pin_4, TTP223B1.VCC, e-radionica1.Vcc
  N3: S1.Pin_1, S1.Pin_2, R1.Pin_0
  N4: LED1.red_anode, R4.Pin_1
  N5: LED1.green_anode, R3.Pin_0
  N6: LED1.blue_anode, R2.Pin_0

custom parts:
  LCD1602-I2C: A standard character display, usually with 2x16 characters. Comes in many colors with LCM1602 IIC attached.
  TTP223B Capacitive Touch Sensor Module: The TTP223B capacitive touch sensor module uses the TTP223B IC. The appropriate voltage is approximately 2 to 5.5 volts.
  TCS230 Color Sensor: TCS230
